# Fritzing sketch 02-3LED (saved by Fritzing 0.9.3b)
breadboards: 1

parts:
  부품1 = Arduino Uno (Rev3)
  LED1 = LED - 5mm [color="Red (633nm)" package="5 mm [THT]"]
  LED2 = LED - 5mm [color="Yellow (595nm)" package="5 mm [THT]"]
  LED3 = LED - 5mm [color="Green (555nm)" package="5 mm [THT]"]
  R1 = Resistor [tolerance=±5% resistance=220 package=THT]
  R2 = Resistor [tolerance=±5% resistance=220 package=THT]
  R3 = Resistor [tolerance=±5% resistance=220 package=THT]

nets:
  N1: 부품1.5V, R1.Pin_1, R2.Pin_1, R3.Pin_1
  N2: 부품1.GND, LED1.cathode, LED2.cathode, LED3.cathode
  N3: LED1.anode, R1.Pin_0
  N4: LED2.anode, R2.Pin_0
  N5: LED3.anode, R3.Pin_0
